# Fritzing sketch PCB (saved by Fritzing 0.9.3b)
perfboards: 2

parts:
  Part1 = Arduino Pro Mini v13
  S1 = Pushbutton [package="[THT]"]
  S2 = Pushbutton [package="[THT]"]
  U1 = TEMPERATURE-SENSOR [package=to-92]
  LED1 = LED - 5mm [color="Green (555nm)" package="5 mm [THT]"]
  LED2 = LED - 5mm [color="Red (633nm)" package="5 mm [THT]"]
  R4 = Resistor [tolerance=±5% resistance=220 package=THT]
  R5 = Resistor [tolerance=±5% resistance=220 package=THT]
  R1 = Rotary Potentiometer (Small) [maximum_resistance=100kΩ package=THT]
  R6 = Resistor [tolerance=±5% resistance=220 package=THT]
  C3 = Ceramic Capacitor [capacitance=100nF package="100 mil [THT, multilayer]"]
  IC2 = MICROCONTROLLER [package=dil28-3-simon]
  C4 = Ceramic Capacitor [capacitance=100nF package="100 mil [THT, multilayer]"]
  XTAL2 = Crystal [frequency="16 Mhz" package=THT]
  R7 = Rotary Potentiometer (Small) [maximum_resistance=100kΩ package=THT]
  LED3 = LED - 5mm [color="Red (633nm)" package="5 mm [THT]"]
  S3 = Pushbutton [package="[THT]"]

nets:
  N1: Part1.A3, S2.Pin_3, S2.Pin_4
  N2: Part1.A2, U1.ADJ
  N3: Part1.A1, S1.Pin_3, S1.Pin_4
  N4: Part1.A0, R1.wiper
  N5: Part1.D10_PWM/SS, LED1.anode
  N6: Part1.D9_PWM, LED2.anode
  N7: S1.Pin_1, S1.Pin_2
  N8: S2.Pin_1, S2.Pin_2
  N9: LED1.cathode, R5.Pin_1
  N10: LED2.cathode, R4.Pin_1
  N11: R6.Pin_0, IC2.VCC, IC2.AVCC
  N12: R6.Pin_1, IC2.PC6(_RESET)
  N13: C3.1, IC2.PB6(XTAL1_TOSC1), XTAL2.pin_1
  N14: IC2.PD2(INT0), S3.Pin_1, S3.Pin_2
  N15: IC2.GND, IC2.AGND
  N16: IC2.PB7(XTAL2_TOSC2), C4.1, XTAL2.pin_0
  N17: IC2.PB2(SS_OC1B), LED3.anode
  N18: IC2.AREF, R7.leg1
  N19: IC2.PC0(ADC0), R7.wiper
  N20: C4.0, S3.Pin_3, S3.Pin_4
  N21: R7.leg2, LED3.cathode
